# Fritzing sketch Fliper RGB (saved by Fritzing 0.9.3b)

parts:
  S17 = Pushbutton [package=THT]
  S18 = Pushbutton [package=THT]
  S19 = Pushbutton [package=THT]
  S20 = Pushbutton [package=THT]
  S21 = Pushbutton [package=THT]
  S22 = Pushbutton [package=THT]
  S23 = Pushbutton [package=THT]
  S24 = Pushbutton [package=THT]
  S25 = Pushbutton [package=THT]
  S26 = Pushbutton [package=THT]
  S27 = Pushbutton [package=THT]
  S28 = Pushbutton [package=THT]
  S29 = Pushbutton [package=THT]
  S30 = Pushbutton [package=THT]
  S31 = Pushbutton [package=THT]
  S32 = Pushbutton [package=THT]
  Part3 = Analog Digital MUX Breakout
  Pro_Micro5 = Pro Micro
  R26 = Rotary Potentiometer (Small) [maximum_resistance=100kΩ package=THT]
  R27 = Rotary Potentiometer (Small) [maximum_resistance=100kΩ package=THT]
  R28 = Rotary Potentiometer (Small) [maximum_resistance=100kΩ package=THT]
  R29 = Rotary Potentiometer (Small) [maximum_resistance=100kΩ package=THT]
  R30 = Rotary Potentiometer (Small) [maximum_resistance=100kΩ package=THT]
  R31 = Rotary Potentiometer (Small) [maximum_resistance=100kΩ package=THT]
  R32 = Rotary Potentiometer (Small) [maximum_resistance=100kΩ package=THT]
  R33 = Rotary Potentiometer (Small) [maximum_resistance=100kΩ package=THT]
  U2 = WS2812 RGB LED strip
  U3 = WS2812 RGB LED strip
  U4 = WS2812 RGB LED strip
  U5 = WS2812 RGB LED strip
  U6 = WS2812 RGB LED strip
  U7 = WS2812 RGB LED strip
  U8 = WS2812 RGB LED strip
  U9 = WS2812 RGB LED strip
  S33 = Pushbutton [package=THT]

nets:
  N1: S17.leg0, S18.leg0, S19.leg0, S20.leg0, S21.leg0, S22.leg0, S23.leg0, S24.leg0, S25.leg0, S26.leg0, S27.leg0, S28.leg0, S29.leg0, S30.leg0, S31.leg0, S32.leg0, U2.GND#0, S33.leg0
  N2: S17.leg1, Part3.C2
  N3: S18.leg1, Part3.C10
  N4: S19.leg1, Part3.C6
  N5: S20.leg1, Part3.C14
  N6: S21.leg1, Part3.C15
  N7: S22.leg1, Part3.C3
  N8: S23.leg1, Part3.C11
  N9: S24.leg1, Part3.C7
  N10: S25.leg1, Part3.C1
  N11: S26.leg1, Part3.C13
  N12: S27.leg1, Part3.C12
  N13: S28.leg1, Part3.C0
  N14: S29.leg1, Part3.C9
  N15: S30.leg1, Part3.C5
  N16: S31.leg1, Part3.C4
  N17: S32.leg1, Part3.C8
  N18: Part3.GND, Part3.EN
  VCC: Part3.VCC, Pro_Micro5.VCC
  N19: Part3.S0, Pro_Micro5.D16/MOSI
  N20: Part3.S1, Pro_Micro5.D14/MISO
  N21: Part3.S2, Pro_Micro5.D15/SCLK
  N22: Part3.S3, Pro_Micro5.D2
  N23: Part3.SIG, Pro_Micro5.D10
  N24: Pro_Micro5.D3, S33.leg1
  N25: Pro_Micro5.D4, R29.wiper
  N26: Pro_Micro5.D5, U2.DIN
  N27: Pro_Micro5.D6, R28.wiper
  N28: Pro_Micro5.D8, R27.wiper
  N29: Pro_Micro5.D9, R26.wiper
  N30: Pro_Micro5.D18/A0, R33.wiper
  N31: Pro_Micro5.D19/A1, R32.wiper
  N32: Pro_Micro5.D20/A2, R31.wiper
  N33: Pro_Micro5.D21/A3, R30.wiper
  N34: Pro_Micro5.GND, R26.leg2, R27.leg2, R28.leg2, R29.leg2, R30.leg2, R31.leg2, R32.leg2, R33.leg2
  N35: R26.leg1, R27.leg1, R28.leg1, R29.leg1, R30.leg1, R31.leg1, R32.leg1, R33.leg1, U2.VCC#1
  N36: U2.GND#4, U3.GND#0
  N37: U2.VCC#5, U3.VCC#1
  N38: U2.DOUT, U3.DIN
  N39: U3.GND#4, U4.GND#0
  N40: U3.VCC#5, U4.VCC#1
  N41: U3.DOUT, U4.DIN
  N42: U4.GND#4, U5.GND#0
  N43: U4.VCC#5, U5.VCC#1
  N44: U4.DOUT, U5.DIN
  N45: U5.GND#4, U6.GND#0
  N46: U5.VCC#5, U6.VCC#1
  N47: U5.DOUT, U6.DIN
  N48: U6.GND#4, U8.GND#0
  N49: U6.VCC#5, U8.VCC#1
  N50: U6.DOUT, U8.DIN
  N51: U7.GND, U9.GND#4
  N52: U7.VCC, U9.VCC#5
  N53: U7.DIN, U9.DOUT
  N54: U8.GND#4, U9.GND#0
  N55: U8.VCC#5, U9.VCC#1
  N56: U8.DOUT, U9.DIN

notes:
  Arduino Pro Micro
  Multiplexer
  CD4067 (breakout)
  Fliper RGB
  by Gustavo Silveira
  A.K.A. Músico Nerd
  gustavosilveira@musiconerd.com
  musiconerd.com
  PS: This schematic is upside down. It's like you were seen the circuit from bellow, in the same way you will solder it.
  Everything.
  Potentiometer b10k
  Led Strip
  ws2812b
  5v
  30 leds per meter

custom parts:
  Pro Micro: The SparkFun Pro Micro is a complete USB-based microcontoller development system, in a very small footprint, capable of implementing many types of projects. All programming can be done via the USB port.
  WS2812 RGB LED strip: WS2812 strip
